# Fritzing sketch RobotGaia IR 4WD (saved by Fritzing 0.9.2b)
breadboards: 1

parts:
  Componente1 = 2A MOTOR SHIELD 9
  Componente2 = Arduino Uno (Rev3)  # not connected
  VCC1 = 4 x AAA Battery Mount
  M1 = DC Motor
  M2 = DC Motor
  M3 = DC Motor
  M4 = DC Motor
  IR1 = TSOP312.., 314.. [part_number="TSOP38238 " package=THT]

nets:
  N1: Componente1.GND#0, VCC1.-
  N2: Componente1.PWRIN, Componente1.D0, VCC1.+
  N3: Componente1.D3, IR1.GND
  N4: Componente1.VIN, IR1.Data
  N5: Componente1.GND#connector1pad-4-5-0-39-8-14, IR1.Vs
  N6: Componente1.M2+, M3.pin_2, M4.pin_2
  N7: Componente1.M2-, M3.pin_1, M4.pin_1
  N8: Componente1.M1+, M1.pin_2, M2.pin_2
  N9: Componente1.M1-, M1.pin_1
